// Digital circuit 4bit_CPU.dig as structural Verilog
module _4bit_CPU (
  input  Clk,
  input  PCInc,
  input  PCLoad,
  input  [3:0] PCDataIn,
  input  [3:0] RamDataIn,
  input  RamReadEnable,
  input  RamWriteEnable,
  input  [1:0] IRCtrl,
  output [3:0] Instruction
);

  wire RAM_p1;
  wire [3:0] RAM_p6;

  // RAM RAM: pin names not known; wires that end beside it: RAM_p1, RamDataIn, Clk, RamReadEnable, RamWriteEnable, RAM_p6
  gp_register A (.Ctrl(2'b00), .In(4'b0000), .Clk(Clk));  // open: Q, Qinv
  gp_register B (.Ctrl(2'b00), .In(4'b0000), .Clk(Clk));  // open: Q, Qinv
  gp_register IR (.Ctrl(IRCtrl), .In(RAM_p6), .Clk(Clk), .Q(Instruction));  // open: Qinv
  // PC PC: pin names not known; wires that end beside it: PCInc, PCLoad, PCDataIn, Clk, RAM_p1
endmodule
