// Digital circuit 4bit_register.dig as structural Verilog
module _4bit_register (
  input  Clk,
  input  [3:0] D,
  output [3:0] Q,
  output [3:0] Qinv
);

  D_FF d_ff_1 (.D(D[0]), .C(Clk), .Q(Q[0]), .nQ(Qinv[0]));
  D_FF d_ff_2 (.D(D[1]), .C(Clk), .Q(Q[1]), .nQ(Qinv[1]));
  D_FF d_ff_3 (.D(D[2]), .C(Clk), .Q(Q[2]), .nQ(Qinv[2]));
  D_FF d_ff_4 (.D(D[3]), .C(Clk), .Q(Q[3]), .nQ(Qinv[3]));
endmodule
