// Digital circuit PC.dig as structural Verilog
module PC (
  input  [3:0] Ctrl,
  input  Clk,
  output [3:0] Out
);

  wire [3:0] _4bit_full_adder_1_p3, _4bit_register_1_q;

  _4bit_register _4bit_register_1 (.Clk(Clk), .D(_4bit_full_adder_1_p3), .Q(_4bit_register_1_q));  // open: Qinv
  // _4bit_full_adder _4bit_full_adder_1: pin names not known; wires that end beside it: _4bit_register_1_q, Ctrl, _4bit_full_adder_1_p3
  Multiplexer #(.Bits(4)) multiplexer_1 (
    .sel(Ctrl[0]), .in_0(_4bit_full_adder_1_p3), .in_1(_4bit_register_1_q), .out(Out));
endmodule
